# Fritzing sketch Contactor Wireless Controlling (saved by Fritzing 0.9.3b)
breadboards: 1

parts:
  U1 = NodeMCU V1.0
  Relay_module1 = Relay Module
  Relay_module2 = Relay Module

nets:
  VIN: U1.3V3, Relay_module1.VIN, Relay_module2.VIN
  GND: U1.GND, Relay_module1.GND, Relay_module2.GND
  N1: Relay_module1.NC, Relay_module2.CO

custom parts:
  NodeMCU V1.0: ESP8266 based NodeMCU
  Relay Module: Design made by me. Relay made by Dynamo Electronics (Colombia). It handles high power required by some electronic components such as motors and light bulbs. This work is licensed under the Creative Commons Attribution-ShareAlike 4.0 International License. To view a copy of this license, visit http://creativecommons.org/licenses/by-sa/4.0/.
